# Fritzing sketch UltimateBatteryTester (saved by Fritzing 0.9.4)
breadboards: 1

parts:
  R4 = Resistor [tolerance=±1% resistance=10k package=THT]
  1602_LCD = LCD screen
  Arduino_Nano = Arduino Nano (Rev3.0)
  R9 = Resistor [tolerance=±1% resistance=47k package=THT]
  1% = Resistor [tolerance=±1% resistance=1 package=THT]
  R12 = Trimmer Potentiometer [maximum_resistance=10kΩ package=THT]
  1%_2 = Resistor [tolerance=±1% resistance=1 package=THT]
  1%_3 = Resistor [tolerance=±1% resistance=1 package=THT]
  N_MOSFET = MOSFET-NCHANNEL [package=to220v]
  2W_1% = Resistor [tolerance=±1% resistance=10 package=THT]
  Battery_under_test = LIPO-110mAh [package=lipo-110]
  N_MOSFET_2 = MOSFET-NCHANNEL [package=to220v]
  1%_4 = Resistor [tolerance=±1% resistance=100k package=THT]
  1%_5 = Resistor [tolerance=±1% resistance=100k package=THT]
  1%_6 = Resistor [tolerance=±1% resistance=100k package=THT]
  1%_7 = Resistor [tolerance=±1% resistance=100k package=THT]
  R13 = Resistor [tolerance=±1% resistance=47k package=THT]
  Buzzer = Piezo Speaker
  Start/stop = Pushbutton [package="[THT]"]

nets:
  N1: R4.Pin_0, Arduino_Nano.A1
  N2: R4.Pin_1, 1%.Pin_0, N_MOSFET.S, N_MOSFET_2.S
  VSS: 1602_LCD.VSS, 1602_LCD.R/W, 1602_LCD.LED-, Arduino_Nano.GND, R9.Pin_1, R12.leg2, 1%_2.Pin_1, Battery_under_test.-, 1%_5.Pin_1, R13.Pin_1, Buzzer.pin1, Start/stop.Pin_1, Start/stop.Pin_2
  5V: 1602_LCD.VDD, 1602_LCD.LED+, Arduino_Nano.5V, R12.leg1
  N3: 1602_LCD.V0, R12.wiper
  N4: 1602_LCD.RS, Arduino_Nano.D7
  N5: 1602_LCD.E, Arduino_Nano.D8
  N6: 1602_LCD.DB4, Arduino_Nano.D3
  N7: 1602_LCD.DB5, Arduino_Nano.D4
  N8: 1602_LCD.DB6, Arduino_Nano.D5
  N9: 1602_LCD.DB7, Arduino_Nano.D6
  N10: Arduino_Nano.D10, Buzzer.pin2
  N11: Arduino_Nano.D11/MOSI, Start/stop.Pin_3, Start/stop.Pin_4
  N12: Arduino_Nano.D12/MISO, N_MOSFET.G, R13.Pin_0
  N13: Arduino_Nano.A3, R9.Pin_0, N_MOSFET_2.G
  N14: Arduino_Nano.A2, 1%_4.Pin_0, 1%_7.Pin_1
  N15: Arduino_Nano.A0, 1%_4.Pin_1, 1%_5.Pin_0, 1%_6.Pin_0, 1%_7.Pin_0
  N16: 1%.Pin_1, 1%_2.Pin_0
  N17: 1%_3.Pin_0, N_MOSFET_2.D
  N18: 1%_3.Pin_1, 2W_1%.Pin_0, Battery_under_test.+, 1%_6.Pin_1
  N19: N_MOSFET.D, 2W_1%.Pin_1
